// Logisim project 8bitcomputer.circ as structural Verilog: 12 circuits, main circuit main
// RO
module main (
  input  in_1,
  input  in_2,
  input  [3:0] in_3,
  input  SEL,
  input  in_5,
  input  [7:0] in_6,
  input  in_7,
  input  in_8,
  input  in_9,
  input  in_10,
  input  [7:0] in_11,
  input  in_12,
  input  in_13,
  input  in_14,
  input  [2:0] in_15,
  input  in_16,
  input  in_17,
  input  in_18,
  input  [3:0] in_19,
  output [6:0] out_20
);

  wire AI, and_1_out, AO, BI, button_1_out, c_RI, CE, CLK, clock_1_out, CO, decoder_1_out0, decoder_1_out1,
       decoder_1_out2, decoder_1_out3, decoder_1_out4, decoder_1_out5, HLT, not_1_out, not_2_out, str;
  wire [3:0] Add, multiplexer_1_out, programcounter_1_output, reg_built_in_2_out_6, rom_2_data_3,
       rom_2_data_4;
  wire [7:0] ALUOUT, AOUT, B, BOUT, I_p_RAM, n1bitregister_4_out_6, rom_2_data, rom_2_data_2;
  wire [14:0] Control_logic;

  Multiplexer #(.width(4), .enable("false")) multiplexer_1 (
    .in0(B[7:4]), .in1(in_19), .out(multiplexer_1_out), .sel(in_18));
  DotMatrix #(.matrixcols(8), .matrixrows(1), .dotshape("circle")) dotmatrix_1 (
    .col0(I_p_RAM[7]), .col1(I_p_RAM[6]), .col2(I_p_RAM[5]), .col3(I_p_RAM[4]), .col4(I_p_RAM[3]),
    .col5(I_p_RAM[2]), .col6(I_p_RAM[1]), .col7(I_p_RAM[0]));
  Multiplexer #(.width(8), .enable("false")) multiplexer_2 (.in0(B), .in1(in_6), .out(I_p_RAM), .sel(in_7));
  Counter #(.width(3), .max('h7)) counter_1 (
    .D(in_15), .Q(out_20[2:0]), .clk(not_1_out), .clr(decoder_1_out5));  // open: load, count, carry
  not not_1 (not_1_out, CLK);
  reg_built_in reg_built_in_1 (
    .in_2(multiplexer_1_out), .in_3(1'b1), .in_4(in_17), .in_5(CLK), .out_6(out_20[6:3]), .Inpur_Enable(in_16));
  LED led_1 (.in(out_20[0]));
  LED led_2 (.in(out_20[1]));
  LED led_3 (.in(out_20[2]));
  Decoder #(.select(3), .enable("false")) decoder_1 (
    .out0(decoder_1_out0), .out1(decoder_1_out1), .out2(decoder_1_out2), .out3(decoder_1_out3),
    .out4(decoder_1_out4), .out5(decoder_1_out5), .sel(out_20[2:0]));  // open: out6, out7
  reg_built_in reg_built_in_2 (
    .in_2(B[3:0]), .in_3(1'b1), .in_4(in_5), .in_5(CLK), .out_6(reg_built_in_2_out_6),
    .Inpur_Enable(Control_logic[1]));
  Button button_1 (.out(button_1_out));
  and and_1 (and_1_out, c_RI, CLK);
  Multiplexer #(.enable("false")) multiplexer_3 (.in0(and_1_out), .in1(Control_logic[2]), .out(str), .sel(in_7));
  DotMatrix #(.matrixcols(8), .matrixrows(1), .dotshape("circle")) dotmatrix_2 (
    .col0(B[7]), .col1(B[6]), .col2(B[5]), .col3(B[4]), .col4(B[3]), .col5(B[2]), .col6(B[1]), .col7(B[0]));
  _1bitregister u_1bitregister_1 (
    .in_1(I_p_RAM), .EN(Control_logic[4]), .WR(Control_logic[5]), .CLOCK(CLK), .CLR(in_9), .out_6(B));
  LED led_4 (.in(decoder_1_out0));
  LED led_5 (.in(decoder_1_out1));
  LED led_6 (.in(decoder_1_out2));
  LED led_7 (.in(decoder_1_out3));
  LED led_8 (.in(decoder_1_out4));
  assign CLK = not_2_out ? clock_1_out : 1'bz;  // Controlled_Buffer controlled_buffer_1
  Clock clock_1 (.out(clock_1_out));
  not not_2 (not_2_out, HLT);
  LED led_9 (.in(B[7]));
  DotMatrix #(.matrixcols(4), .matrixrows(1), .dotshape("circle")) dotmatrix_3 (
    .col0(Add[3]), .col1(Add[2]), .col2(Add[1]), .col3(Add[0]));
  Multiplexer #(.width(4), .enable("false")) multiplexer_4 (
    .in0(reg_built_in_2_out_6), .in1(in_3), .out(Add), .sel(in_7));
  DotMatrix #(.matrixcols(8), .matrixrows(1), .dotshape("circle")) dotmatrix_4 (
    .col0(B[7]), .col1(B[6]), .col2(B[5]), .col3(B[4]), .col4(B[3]), .col5(B[2]), .col6(B[1]), .col7(B[0]));
  RAM #(.addrWidth(4), .bus("separate")) ram_1 (
    .addr(Add), .din(I_p_RAM), .data(B), .str(button_1_out), .sel(SEL), .clk(CLK), .ld(Control_logic[3]),
    .clr(in_5));
  DotMatrix #(.matrixcols(15), .matrixrows(1), .dotshape("circle")) dotmatrix_5 (
    .col0(Control_logic[14]), .col1(CO), .col2(CE), .col3(Control_logic[11]), .col4(BI),
    .col5(Control_logic[9]), .col6(Control_logic[8]), .col7(AO), .col8(AI), .col9(Control_logic[5]),
    .col10(Control_logic[4]), .col11(Control_logic[3]), .col12(Control_logic[2]), .col13(Control_logic[1]),
    .col14(Control_logic[0]));
  LED led_10 (.in(B[5]));
  LED led_11 (.in(B[4]));
  LED led_12 (.in(B[6]));
  LED led_13 (.in(B[3]));
  assign B = AO ? AOUT : 8'bz;  // Controlled_Buffer controlled_buffer_2
  assign B = in_10 ? in_11 : 8'bz;  // Controlled_Buffer controlled_buffer_3
  LED led_14 (.in(B[1]));
  LED led_15 (.in(B[2]));
  LED led_16 (.in(B[0]));
  ROM #(.addrWidth(7), .dataWidth(15)) rom_1 (
    .addr(out_20),
    .data({Control_logic[14], CO, CE, Control_logic[11], BI, Control_logic[9:8], AO, AI, Control_logic[5:0]}));  // open: sel
  alu_main alu_main_1 (
    .SUB(Control_logic[9]), .EN(Control_logic[8]), .in_3(BOUT), .in_4(AOUT), .Result(B), .Result_2(ALUOUT));
  _1bitregister u_1bitregister_2 (.in_1(B), .EN(1'b1), .WR(AI), .CLOCK(CLK), .CLR(in_2), .out_6(AOUT));
  _1bitregister u_1bitregister_3 (.in_1(B), .EN(1'b1), .WR(BI), .CLOCK(CLK), .CLR(in_8), .out_6(BOUT));
  LED led_17 (.in(AOUT[7]));
  LED led_18 (.in(BOUT[7]));
  _1bitregister u_1bitregister_4 (
    .in_1(B), .EN(1'b1), .WR(Control_logic[11]), .CLOCK(CLK), .CLR(in_12), .out_6(n1bitregister_4_out_6));
  LED led_19 (.in(AOUT[6]));
  LED led_20 (.in(AOUT[3]));
  LED led_21 (.in(AOUT[4]));
  LED led_22 (.in(AOUT[5]));
  LED led_23 (.in(BOUT[3]));
  LED led_24 (.in(BOUT[5]));
  LED led_25 (.in(BOUT[6]));
  LED led_26 (.in(BOUT[4]));
  Multiplexer #(.enable("false")) multiplexer_5 (.in0(Control_logic[0]), .in1(in_14), .out(HLT), .sel(in_13));
  LED led_27 (.in(AOUT[1]));
  LED led_28 (.in(AOUT[2]));
  LED led_29 (.in(AOUT[0]));
  LED led_30 (.in(ALUOUT[6]));
  LED led_31 (.in(ALUOUT[7]));
  LED led_32 (.in(ALUOUT[4]));
  LED led_33 (.in(ALUOUT[5]));
  LED led_34 (.in(BOUT[1]));
  LED led_35 (.in(BOUT[0]));
  LED led_36 (.in(BOUT[2]));
  ROM #(.dataWidth(24)) rom_2 (
    .addr(n1bitregister_4_out_6), .data({rom_2_data_4, rom_2_data_3, rom_2_data_2, rom_2_data}));  // open: sel
  LED led_37 (.in(ALUOUT[1]));
  LED led_38 (.in(ALUOUT[0]));
  LED led_39 (.in(ALUOUT[3]));
  LED led_40 (.in(ALUOUT[2]));
  Hex_Digit_Display hex_digit_display_1 (.value(rom_2_data_3));  // open: dp
  Hex_Digit_Display hex_digit_display_2 (.value(rom_2_data_2[3:0]));  // open: dp
  Hex_Digit_Display hex_digit_display_3 (.value(rom_2_data[3:0]));  // open: dp
  assign B[3:0] = CO ? programcounter_1_output : 4'bz;  // Controlled_Buffer Output_enable
  programcounter programcounter_1 (
    .Jump(Control_logic[14]), .\input (B[3:0]), .Count_Enable(CE), .Clock(CLK), .Clear(in_1),
    .Output(programcounter_1_output));

  // Other names for the same wires on the sheet: CLR_A = in_2; CLR_B = in_8; CLR_IR = in_9; CLR_PC = in_1;
  //   CLR_R = in_5; MI = Control_logic[1]; RI = Control_logic[2]; RO = Control_logic[3]; IO = Control_logic[4];
  //   II = Control_logic[5]; Control_logic (some bits) = {CO, CE, BI, AO, AI}; EO = Control_logic[8];
  //   SUB = Control_logic[9]; OI = Control_logic[11]; Jump = Control_logic[14]; M_A = in_7; M_A_Input[3:0] = in_3;
  //   B1[3:0] = B[3:0]; Pc[7:0] = B; Pc2[7:0] = B; B2[3:0] = B[7:4]; Instruc[3:0] = B[7:4]

  // Notes on the sheet:
  //   WR
  //   ENABLE
  //   BUS
  //   WR
  //   WR
  //   contents of rom_1 (hex, n*v repeats v):
  //   2002 1028 6*0 2002 1028 12 48 4*0 2002 1028 12 408 140 0 0 0 2002 1028 6*0 2002 1028 6*0 2002 1028
  //   6*0 2002 1028 6*0 2002 1028 6*0 2002 1028 6*0 2002 1028 6*0 2002 1028 6*0 2002 1028 6*0 2002 1028
  //   6*0 2002 1028 6*0 2002 1028 480 5*0 2002 1028 1
  //   FIRST 4 
  //   NEXT 4
  //   REGISTER A
  //   REGISTER B
  //   ENABLE
  //   ENABLE
  //   SUB
  //   ENABLE
  //   contents of rom_2 (hex, n*v repeats v):
  //   0 1 2 3 4 5 6 7 8 9 100 101 102 103 104 105 106 107 108 109 200 201 202 203 204 205 206 207 208 209
  //   300 301 302 303 304 305 306 307 308 309 400 401 402 403 404 405 406 407 408 409 500 501 502 503 504
  //   505 506 507 508 509 600 601 602 603 604 605 606 607 608 609 700 701 702 703 704 705 706 707 708 709
  //   800 801 802 803 804 805 806 807 808 809 900 901 902 903 904 905 906 907 908 909 10000 10001 10002
  //   10003 10004 10005 10006 10007 10008 10009 10100 10101 10102 10103 10104 10105 10106 10107 10108
  //   10109 10200 10201 10202 10203 10204 10205 10206 10207 10208 10209 10300 10301 10302 10303 10304
  //   10305 10306 10307 10308 10309 10400 10401 10402 10403 10404 10405 10406 10407 10408 10409 10500
  //   10501 10502 10503 10504 10505 10506 10507 10508 10509 10600 10601 10602 10603 10604 10605 10606
  //   10607 10608 10609 10700 10701 10702 10703 10704 10705 10706 10707 10708 10709 10800 10801 10802
  //   10803 10804 10805 10806 10807 10808 10809 10900 10901 10902 10903 10904 10905 10906 10907 10908
  //   10909 20000 20001 20002 20003 20004 20005 20006 20007 20008 20009 20100 20101 20102 20103 20104
  //   20105 20106 20107 20108 20109 20200 20201 20202 20203 20204 20205 20206 20207 20208 20209 20300
  //   20301 20302 20303 20304 20305 20306 20307 20308 20309 20400 20401 20402 20403 20404 20405 20406
  //   20407 20408 20409 20500 20501 20502 20503 20504 20505
  //   CONTROL SIGNALS
endmodule

module full__adder (
  input  A,
  input  B,
  input  Cin,
  output S,
  output Co
);

  wire and_1_out, and_2_out, and_3_out, and_4_out, and_5_out, and_6_out, not_1_out, not_2_out, not_3_out,
       not_4_out, or_1_out;

  not not_1 (not_1_out, B);
  not not_2 (not_2_out, A);
  and and_1 (and_1_out, not_1_out, A);
  and and_2 (and_2_out, B, not_2_out);
  or or_1 (or_1_out, and_1_out, and_2_out);
  and and_3 (and_3_out, A, B);
  not not_3 (not_3_out, Cin);
  not not_4 (not_4_out, or_1_out);
  and and_4 (and_4_out, Cin, or_1_out);
  and and_5 (and_5_out, not_3_out, or_1_out);
  and and_6 (and_6_out, not_4_out, Cin);
  or or_2 (Co, and_4_out, and_3_out);
  or or_3 (S, and_5_out, and_6_out);

  // Notes on the sheet:
  //   A
  //   B
  //   Cin
  //   S
  //   Co
endmodule

module _4_b (
  input  in_1,
  input  in_2,
  input  in_3,
  input  in_4,
  input  in_5,
  input  B0,
  input  in_7,
  input  in_8,
  input  in_9,
  output out_10,
  output out_11,
  output out_12,
  output out_13,
  output out_14
);

  wire and_1_out, and_4_out, and_5_out, and_6_out, and_9_out, and_10_out, and_11_out, and_12_out, and_13_out,
       and_14_out, C0, C1, C2, G0, G1, G2, G3, P0, P1, P2, P3;

  and and_1 (and_1_out, P0, in_5);
  xor xor_1 (P0, in_1, B0);
  xor xor_2 (P1, in_2, in_7);
  and and_2 (G0, in_1, B0);
  and and_3 (G1, in_2, in_7);
  or or_1 (C0, and_1_out, G0);
  and and_4 (and_4_out, in_5, P2, P0, P1);
  and and_5 (and_5_out, P1, P2, G0);
  and and_6 (and_6_out, P2, G1);
  or or_2 (C2, and_4_out, G2, and_6_out, and_5_out);
  xor xor_3 (P2, in_3, in_8);
  xor xor_4 (P3, in_4, in_9);
  and and_7 (G2, in_3, in_8);
  and and_8 (G3, in_4, in_9);
  and and_9 (and_9_out, P0, P1, in_5);
  and and_10 (and_10_out, P1, G0);
  and and_11 (and_11_out, in_5, P0, P1, P2, P3);
  and and_12 (and_12_out, P3, P2, P1, G0);
  and and_13 (and_13_out, P3, P2, G1);
  and and_14 (and_14_out, P3, G2);
  or or_3 (C1, and_9_out, G1, and_10_out);
  or or_4 (out_14, G3, and_11_out, and_12_out, and_13_out, and_14_out);
  full__adder full_adder_1 (.A(in_1), .B(B0), .Cin(in_5), .S(out_10));  // open: Co
  full__adder full_adder_2 (.A(in_4), .B(in_9), .Cin(C2), .S(out_13));  // open: Co
  full__adder full_adder_3 (.A(in_2), .B(in_7), .Cin(C0), .S(out_11));  // open: Co
  full__adder full_adder_4 (.A(in_3), .B(in_8), .Cin(C1), .S(out_12));  // open: Co

  // Other names for the same wires on the sheet: A0 = in_1; A1 = in_2; A2 = in_3; A3 = in_4; B1 = in_7; B2 = in_8;
  //   B3 = in_9; Cin = in_5; Cout = out_14; S0 = out_10; S1 = out_11; S2 = out_12; S3 = out_13

  // Notes on the sheet:
  //   C0
  //   C2
  //   generating variables
  //   C1
  //   Cout
  //   FOR BIT 0
  //   FOR BIT 3
  //   Predicting Carries
  //   Implementation
  //   FOR BIT 1
  //   FOR BIT 2
endmodule

module alu_main (
  input  SUB,
  input  EN,
  input  [7:0] in_3,
  input  [7:0] in_4,
  output [7:0] Result,
  output [7:0] Result_2
);

  wire n4_b_1_out_14, xor_1_out, xor_2_out, xor_3_out, xor_4_out, xor_5_out, xor_6_out, xor_7_out, xor_8_out;

  xor xor_1 (xor_1_out, in_3[0], SUB);
  xor xor_2 (xor_2_out, in_3[1], SUB);
  xor xor_3 (xor_3_out, in_3[2], SUB);
  xor xor_4 (xor_4_out, in_3[3], SUB);
  xor xor_5 (xor_5_out, in_3[4], SUB);
  xor xor_6 (xor_6_out, in_3[5], SUB);
  xor xor_7 (xor_7_out, in_3[6], SUB);
  xor xor_8 (xor_8_out, in_3[7], SUB);
  _4_b u_4_b_1 (
    .in_1(in_4[0]), .in_2(in_4[1]), .in_3(in_4[2]), .in_4(in_4[3]), .B0(xor_1_out), .in_7(xor_2_out),
    .in_8(xor_3_out), .in_9(xor_4_out), .out_10(Result_2[0]), .out_11(Result_2[1]), .out_12(Result_2[2]),
    .out_13(Result_2[3]), .out_14(n4_b_1_out_14), .in_5(SUB));
  _4_b u_4_b_2 (
    .in_1(in_4[4]), .in_2(in_4[5]), .in_3(in_4[6]), .in_4(in_4[7]), .B0(xor_5_out), .in_7(xor_6_out),
    .in_8(xor_7_out), .in_9(xor_8_out), .out_10(Result_2[4]), .out_11(Result_2[5]), .out_12(Result_2[6]),
    .out_13(Result_2[7]), .in_5(n4_b_1_out_14));  // open: out_14
  assign Result[0] = EN ? Result_2[0] : 1'bz;  // Controlled_Buffer controlled_buffer_1
  assign Result[1] = EN ? Result_2[1] : 1'bz;  // Controlled_Buffer controlled_buffer_2
  assign Result[2] = EN ? Result_2[2] : 1'bz;  // Controlled_Buffer controlled_buffer_3
  assign Result[3] = EN ? Result_2[3] : 1'bz;  // Controlled_Buffer controlled_buffer_4
  assign Result[4] = EN ? Result_2[4] : 1'bz;  // Controlled_Buffer controlled_buffer_5
  assign Result[5] = EN ? Result_2[5] : 1'bz;  // Controlled_Buffer controlled_buffer_6
  assign Result[6] = EN ? Result_2[6] : 1'bz;  // Controlled_Buffer controlled_buffer_7
  assign Result[7] = EN ? Result_2[7] : 1'bz;  // Controlled_Buffer controlled_buffer_8

  // Other names for the same wires on the sheet: ENABLE = EN

  // Notes on the sheet:
  //   REGISTER B
  //   REGISTER A
  //   ALU
  //   RESULT
endmodule

module reg_built_in (
  input  Inpur_Enable,
  input  [3:0] in_2,
  input  in_3,
  input  in_4,
  input  in_5,
  output [3:0] out_6
);

  wire [3:0] controlled_buffer_1_out;

  assign controlled_buffer_1_out = Inpur_Enable ? in_2 : 4'bz;  // Controlled_Buffer controlled_buffer_1
  Register #(.width(4)) register_1 (.D(controlled_buffer_1_out), .en(in_3), .Q(out_6), .clk(in_5), .clr(in_4));
endmodule

module RAM_BUILT_IN (
  input  [7:0] in_1,
  input  [3:0] M_In,
  input  SEL,
  input  in_4,
  input  [7:0] in_5
);

  wire and_1_out, c_RI, CLK, M_A, MI, RI, RO, str;
  wire [3:0] Add, reg_built_in_1_out_6;
  wire [7:0] I_p_RAM, ram_1_data;

  DotMatrix #(.matrixcols(8), .matrixrows(1), .dotshape("circle")) dotmatrix_1 (
    .col0(I_p_RAM[7]), .col1(I_p_RAM[6]), .col2(I_p_RAM[5]), .col3(I_p_RAM[4]), .col4(I_p_RAM[3]),
    .col5(I_p_RAM[2]), .col6(I_p_RAM[1]), .col7(I_p_RAM[0]));
  Multiplexer #(.width(8), .enable("false")) multiplexer_1 (.in0(in_1), .in1(in_5), .out(I_p_RAM), .sel(M_A));
  reg_built_in reg_built_in_1 (
    .in_2(in_1[3:0]), .in_3(1'b1), .in_4(in_4), .in_5(CLK), .out_6(reg_built_in_1_out_6), .Inpur_Enable(MI));
  and and_1 (and_1_out, c_RI, CLK);
  DotMatrix #(.matrixcols(4), .matrixrows(1), .dotshape("circle")) dotmatrix_2 (
    .col0(Add[3]), .col1(Add[2]), .col2(Add[1]), .col3(Add[0]));
  Multiplexer #(.enable("false")) multiplexer_2 (.in0(and_1_out), .in1(RI), .out(str), .sel(M_A));
  LED led_1 ();  // open: in
  LED led_2 ();  // open: in
  Multiplexer #(.width(4), .enable("false")) multiplexer_3 (
    .in0(reg_built_in_1_out_6), .in1(M_In), .out(Add), .sel(M_A));
  DotMatrix #(.matrixcols(8), .matrixrows(1), .dotshape("circle")) dotmatrix_3 (
    .col0(ram_1_data[7]), .col1(ram_1_data[6]), .col2(ram_1_data[5]), .col3(ram_1_data[4]),
    .col4(ram_1_data[3]), .col5(ram_1_data[2]), .col6(ram_1_data[1]), .col7(ram_1_data[0]));
  RAM #(.addrWidth(4), .bus("separate")) ram_1 (
    .addr(Add), .din(I_p_RAM), .data(ram_1_data), .str(str), .sel(SEL), .clk(CLK), .ld(RO), .clr(in_4));
  LED led_3 ();  // open: in

  // Other names for the same wires on the sheet: B[7:0] = in_1; B1[3:0] = in_1[3:0]; B2[3:0] = in_1[7:4];
  //   CLR_R = in_4; M_A_Input[3:0] = M_In
endmodule

module b2d (
  input  [7:0] in_1
);

  wire clock_1_out;
  wire [7:0] counter_1_q;
  wire [23:0] rom_1_data;

  Clock clock_1 (.out(clock_1_out));
  Counter counter_1 (.D(in_1), .Q(counter_1_q), .clk(clock_1_out));  // open: load, count, carry, clr
  ROM #(.dataWidth(24)) rom_1 (.addr(counter_1_q), .data(rom_1_data));  // open: sel
  Hex_Digit_Display hex_digit_display_1 (.value(rom_1_data[19:16]));  // open: dp
  Hex_Digit_Display hex_digit_display_2 (.value(rom_1_data[11:8]));  // open: dp
  Hex_Digit_Display hex_digit_display_3 (.value(rom_1_data[3:0]));  // open: dp

  // Notes on the sheet:
  //   contents of rom_1 (hex, n*v repeats v):
  //   0 1 2 3 4 5 6 7 8 9 100 101 102 103 104 105 106 107 108 109 200 201 202 203 204 205 206 207 208 209
  //   300 301 302 303 304 305 306 307 308 309 400 401 402 403 404 405 406 407 408 409 500 501 502 503 504
  //   505 506 507 508 509 600 601 602 603 604 605 606 607 608 609 700 701 702 703 704 705 706 707 708 709
  //   800 801 802 803 804 805 806 807 808 809 900 901 902 903 904 905 906 907 908 909 10000 10001 10002
  //   10003 10004 10005 10006 10007 10008 10009 10100 10101 10102 10103 10104 10105 10106 10107 10108
  //   10109 10200 10201 10202 10203 10204 10205 10206 10207 10208 10209 10300 10301 10302 10303 10304
  //   10305 10306 10307 10308 10309 10400 10401 10402 10403 10404 10405 10406 10407 10408 10409 10500
  //   10501 10502 10503 10504 10505 10506 10507 10508 10509 10600 10601 10602 10603 10604 10605 10606
  //   10607 10608 10609 10700 10701 10702 10703 10704 10705 10706 10707 10708 10709 10800 10801 10802
  //   10803 10804 10805 10806 10807 10808 10809 10900 10901 10902 10903 10904 10905 10906 10907 10908
  //   10909 20000 20001 20002 20003 20004 20005 20006 20007 20008 20009 20100 20101 20102 20103 20104
  //   20105 20106 20107 20108 20109 20200 20201 20202 20203 20204 20205 20206 20207 20208 20209 20300
  //   20301 20302 20303 20304 20305 20306 20307 20308 20309 20400 20401 20402 20403 20404 20405 20406
  //   20407 20408 20409 20500 20501 20502 20503 20504 20505
endmodule

module a1 (
  input  LOAD,
  input  I_P,
  input  CLK,
  input  CLR,
  output out_5
);

  wire and_1_out, and_2_out, not_1_out, or_1_out;

  Pull_Resistor #(.pull(1)) pull_resistor_1 (.node(I_P));
  and and_1 (and_1_out, out_5, not_1_out);
  not not_1 (not_1_out, LOAD);
  and and_2 (and_2_out, LOAD, I_P);
  reg_part reg_part_1 (.CLR(CLR), .I_P(or_1_out), .CLK(CLK), .out_4(out_5));  // open: out_5
  or or_1 (or_1_out, and_1_out, and_2_out);
endmodule

module _1bitregister (
  input  [7:0] in_1,
  input  EN,
  input  WR,
  input  CLOCK,
  input  CLR,
  output [7:0] out_6
);

  wire a1_1_out_5, a1_2_out_5, a1_3_out_5, a1_4_out_5, a1_5_out_5, a1_6_out_5, a1_7_out_5, a1_8_out_5;

  a1 a1_1 (.LOAD(WR), .I_P(in_1[7]), .CLK(CLOCK), .CLR(CLR), .out_5(a1_1_out_5));
  a1 a1_2 (.LOAD(WR), .I_P(in_1[6]), .CLK(CLOCK), .CLR(CLR), .out_5(a1_2_out_5));
  a1 a1_3 (.LOAD(WR), .I_P(in_1[5]), .CLK(CLOCK), .CLR(CLR), .out_5(a1_3_out_5));
  a1 a1_4 (.LOAD(WR), .I_P(in_1[4]), .CLK(CLOCK), .CLR(CLR), .out_5(a1_4_out_5));
  a1 a1_5 (.LOAD(WR), .I_P(in_1[3]), .CLK(CLOCK), .CLR(CLR), .out_5(a1_5_out_5));
  a1 a1_6 (.LOAD(WR), .I_P(in_1[2]), .CLK(CLOCK), .CLR(CLR), .out_5(a1_6_out_5));
  a1 a1_7 (.LOAD(WR), .I_P(in_1[1]), .CLK(CLOCK), .CLR(CLR), .out_5(a1_7_out_5));
  a1 a1_8 (.LOAD(WR), .I_P(in_1[0]), .CLK(CLOCK), .CLR(CLR), .out_5(a1_8_out_5));
  assign out_6[7] = EN ? a1_1_out_5 : 1'bz;  // Controlled_Buffer controlled_buffer_1
  assign out_6[6] = EN ? a1_2_out_5 : 1'bz;  // Controlled_Buffer controlled_buffer_2
  assign out_6[5] = EN ? a1_3_out_5 : 1'bz;  // Controlled_Buffer controlled_buffer_3
  assign out_6[4] = EN ? a1_4_out_5 : 1'bz;  // Controlled_Buffer controlled_buffer_4
  assign out_6[3] = EN ? a1_5_out_5 : 1'bz;  // Controlled_Buffer controlled_buffer_5
  assign out_6[2] = EN ? a1_6_out_5 : 1'bz;  // Controlled_Buffer controlled_buffer_6
  assign out_6[1] = EN ? a1_7_out_5 : 1'bz;  // Controlled_Buffer controlled_buffer_7
  assign out_6[0] = EN ? a1_8_out_5 : 1'bz;  // Controlled_Buffer controlled_buffer_8

  // Notes on the sheet:
  //   INPUT
  //   LOAD
endmodule

module reg_part (
  input  CLR,
  input  I_P,
  input  CLK,
  output out_4,
  output out_5
);

  wire and_1_out, and_2_out, and_3_out, not_1_out, not_2_out, not_3_out, not_4_out;

  not not_1 (not_1_out, CLK);
  not not_2 (not_2_out, not_1_out);
  not not_3 (not_3_out, I_P);
  and and_1 (and_1_out, CLK, not_4_out);
  not not_4 (not_4_out, not_2_out);
  and and_2 (and_2_out, not_3_out, and_1_out);
  and and_3 (and_3_out, and_1_out, I_P);
  nor nor_1 (out_4, and_2_out, CLR, out_5);
  nor nor_2 (out_5, out_4, and_3_out);
endmodule

module programcounter (
  input  Jump,
  input  [3:0] \input ,
  input  Count_Enable,
  input  Clock,
  input  Clear,
  output [3:0] Output
);

  Counter #(.width(4), .max('hf), .ongoal("stay")) counter_1 (
    .load(Jump), .D(\input ), .count(Count_Enable), .Q(Output), .clk(Clock), .clr(Clear));  // open: carry
endmodule

module output_reg (
  input  [6:0] in_1,
  input  in_2,
  input  in_3,
  input  in_4,
  output [6:0] out_5
);

  Register #(.width(7)) register_1 (.D(in_1), .en(in_2), .Q(out_5), .clk(in_3), .clr(in_4));
endmodule
